// Logisim project log.circ as structural Verilog: 7 circuits, main circuit motherboard
module motherboard (
  input  [7:0] in_1
);

  wire clock_1_out;
  wire [1:0] cpu_1_ramctrl;
  wire [7:0] cpu_1_dataout;
  wire [15:0] cpu_1_ramout;

  CPU cpu_1 (
    .ramOUT(cpu_1_ramout), .dataout(cpu_1_dataout), .datain(cpu_1_dataout), .ramctrl(cpu_1_ramctrl),
    .clk(clock_1_out));  // open: out_3
  Clock clock_1 (.out(clock_1_out));
  // Probe on in_1
  // Probe on cpu_1_ramout
  // Probe on cpu_1_dataout
  RAM #(.addrWidth(16)) ram_1 (
    .addr(cpu_1_ramout), .data(cpu_1_dataout), .clk(cpu_1_ramctrl[0]), .ld(cpu_1_ramctrl[1]));  // open: sel, clr
  // Probe on cpu_1_dataout
  TTY tty_1 ();  // open: data, clk, we, clr
endmodule

module FLG (
  input  [3:0] in_1,
  input  [1:0] in_2,
  output t_f
);

  wire [3:0] and_1_out, decoder_1_out0;

  Decoder #(.select(2), .disabled(0), .enable("false")) decoder_1 (
    .out0(decoder_1_out0[0]), .out1(decoder_1_out0[1]), .out2(decoder_1_out0[2]), .out3(decoder_1_out0[3]),
    .sel(in_2));
  Pull_Resistor pull_resistor_1 (.node(in_1));
  Pull_Resistor pull_resistor_2 (.node(decoder_1_out0));
  // Probe on and_1_out
  assign and_1_out = in_1 & decoder_1_out0;  // AND_Gate and_1, 4 bits wide
  or or_1 (t_f, and_1_out[0], and_1_out[1], and_1_out[2], and_1_out[3]);
endmodule

module ALU (
  input  [2:0] in_1,
  input  [7:0] A,
  input  [7:0] B,
  input  [3:0] in_4,
  input  en,
  output [7:0] out_6,
  output [3:0] out_7
);

  wire adder_1_cout, and_2_out, and_3_out, not_2_out, not_3_out, not_4_out, not_5_out, not_6_out,
       subtractor_1_bout;
  wire [3:0] bitadder_1_out;
  wire [7:0] adder_1_out, and_1_out, not_1_out, or_1_out, subtractor_1_out, undriven, undriven_2, xor_1_out;

  Pull_Resistor pull_resistor_1 (.node(A));
  assign not_1_out = ~A;  // NOT_Gate not_1, 8 bits wide
  Adder adder_1 (.a(A), .b(B), .out(adder_1_out), .cin(in_4[0]), .cout(adder_1_cout));
  assign out_7[0] = and_3_out ? adder_1_cout : 1'bz;  // Controlled_Buffer controlled_buffer_1
  Subtractor subtractor_1 (.a(A), .b(B), .out(subtractor_1_out), .bin(in_4[0]), .bout(subtractor_1_bout));
  assign out_7[0] = and_2_out ? subtractor_1_bout : 1'bz;  // Controlled_Buffer controlled_buffer_2
  assign and_1_out = A & B;  // AND_Gate and_1, 8 bits wide
  assign or_1_out = A | B;  // OR_Gate or_1, 8 bits wide
  assign xor_1_out = A ^ B;  // XOR_Gate xor_1, 8 bits wide
  Comparator comparator_1 (.a(A), .b(B), .gt(out_7[1]), .eq(out_7[2]));  // open: lt
  nor nor_1 (out_7[3], bitadder_1_out[0], bitadder_1_out[1], bitadder_1_out[2], bitadder_1_out[3]);
  BitAdder bitadder_1 (.in0(A), .out(bitadder_1_out));
  and and_2 (and_2_out, in_1[0], not_2_out, not_3_out);
  not not_2 (not_2_out, in_1[1]);
  not not_3 (not_3_out, in_1[2]);
  not not_4 (not_4_out, in_1[0]);
  and and_3 (and_3_out, not_4_out, not_5_out, not_6_out);
  not not_5 (not_5_out, in_1[1]);
  not not_6 (not_6_out, in_1[2]);
  Multiplexer #(.select(3), .width(8)) multiplexer_1 (
    .in0(adder_1_out), .in1(subtractor_1_out), .in2(and_1_out), .in3(or_1_out), .in4(xor_1_out),
    .in5(not_1_out), .in6(undriven), .in7(undriven_2), .out(out_6), .sel(in_1), .en(en));
endmodule

module Timer (
  input  sRST,
  input  clk,
  output [3:0] ct,
  output e,
  output s
);

  wire and_1_out, decoder_1_out0, decoder_1_out1, decoder_1_out2, not_1_out, t_ff_1_q;
  wire [1:0] t_ff_2_q;

  not not_1 (not_1_out, clk);
  T_Flip_Flop t_ff_1 (.clk(sRST), .T(sRST), .Q(t_ff_1_q), .reset(decoder_1_out0));  // open: Qn, preset, en
  T_Flip_Flop t_ff_2 (.clk(not_1_out), .T(not_1_out), .Q(t_ff_2_q[0]));  // open: Qn, preset, reset, en
  T_Flip_Flop t_ff_3 (.clk(clk), .T(clk), .Q(t_ff_2_q[1]));  // open: Qn, preset, reset, en
  and and_1 (and_1_out, t_ff_1_q, decoder_1_out0);
  Decoder #(.select(2), .disabled(0), .enable("false")) decoder_1 (
    .out0(decoder_1_out0), .out1(decoder_1_out1), .out2(decoder_1_out2), .out3(s), .sel(t_ff_2_q));
  Counter #(.width(4), .max('hf)) counter_1 (
    .Q(ct), .clk(decoder_1_out0), .clr(and_1_out));  // open: load, D, count, carry
  or or_1 (e, decoder_1_out1, decoder_1_out2, s);
endmodule

module CPU (
  input  [7:0] datain,
  input  clk,
  output [7:0] out_3,
  output [7:0] dataout,
  output [15:0] ramOUT,
  output [1:0] ramctrl
);

  wire and_1_out, and_2_out, control_unit_1_e16tr, control_unit_1_ealu, control_unit_1_sbus,
       control_unit_1_sin, control_unit_1_srst, control_unit_1_stmp, timer_1_e, timer_1_s;
  wire [1:0] control_unit_1_e_s_acc, control_unit_1_e_s_flg, control_unit_1_e_s_ra, control_unit_1_e_s_sp,
       control_unit_1_ramen;
  wire [2:0] control_unit_1_op, control_unit_1_reg;
  wire [3:0] alu_1_out_7, control_unit_1_e_s_ct_ld_adb, control_unit_1_e_s_ct_ld_pc,
       control_unit_1_hl_e_s_hl, controlled_buffer_2_out, register_3_q, timer_1_ct;
  wire [7:0] controlled_buffer_1_out, register_1_q, register_2_q, register_4_q;

  assign controlled_buffer_1_out = control_unit_1_e_s_acc[1] ? register_1_q : 8'bz;  // Controlled_Buffer controlled_buffer_1
  Register #(.trigger("falling")) register_1 (
    .D(controlled_buffer_1_out), .Q(register_1_q), .clk(control_unit_1_e_s_acc[0]));  // open: en, clr
  Register register_2 (.D(controlled_buffer_1_out), .Q(register_2_q), .clk(control_unit_1_stmp));  // open: en, clr
  Register #(.width(4)) register_3 (
    .D(alu_1_out_7), .Q(register_3_q), .clk(control_unit_1_e_s_flg[1]));  // open: en, clr
  assign controlled_buffer_2_out = control_unit_1_e_s_flg[0] ? register_3_q : 4'bz;  // Controlled_Buffer controlled_buffer_2
  ALU alu_1 (
    .in_4(controlled_buffer_2_out), .A(register_1_q), .B(register_2_q), .in_1(control_unit_1_op),
    .out_6(controlled_buffer_1_out), .out_7(alu_1_out_7), .en(control_unit_1_ealu));
  // Probe on controlled_buffer_1_out
  control_unit control_unit_1 (
    .e(timer_1_e), .s(timer_1_s), .ct(timer_1_ct), .e_s_ACC(control_unit_1_e_s_acc),
    .sTMP(control_unit_1_stmp), .eALU(control_unit_1_ealu), .e_s_FLG(control_unit_1_e_s_flg),
    .OP(control_unit_1_op), .sRST(control_unit_1_srst), .e_s_ct_LD_ADB(control_unit_1_e_s_ct_ld_adb),
    .e_s_ct_ld_PC(control_unit_1_e_s_ct_ld_pc), .e_s_SP(control_unit_1_e_s_sp),
    .hl_e_s_HL(control_unit_1_hl_e_s_hl), .e_s_RA(control_unit_1_e_s_ra), .e_s_RAM(ramctrl),
    .sIN(control_unit_1_sin), .INST(register_4_q), .REG(control_unit_1_reg),
    .flg_in(controlled_buffer_2_out), .sBUS(control_unit_1_sbus), .e16tr(control_unit_1_e16tr),
    .ramen(control_unit_1_ramen));
  Timer timer_1 (.sRST(control_unit_1_srst), .ct(timer_1_ct), .e(timer_1_e), .s(timer_1_s), .clk(clk));
  Register register_4 (.D(controlled_buffer_1_out), .Q(register_4_q), .clk(control_unit_1_sin));  // open: en, clr
  Register register_5 (.D(controlled_buffer_1_out), .Q(out_3), .clk(control_unit_1_sbus));  // open: en, clr
  regfile regfile_1 (
    .in_1(controlled_buffer_1_out), .out_9(controlled_buffer_1_out), .in_3(control_unit_1_e_s_ra),
    .in_5(control_unit_1_reg), .adb(control_unit_1_e_s_ct_ld_adb), .pc(control_unit_1_e_s_ct_ld_pc),
    .sp(control_unit_1_e_s_sp), .out_10(ramOUT), .in_2(control_unit_1_hl_e_s_hl), .e16tr(control_unit_1_e16tr));
  assign dataout = and_2_out ? controlled_buffer_1_out : 8'bz;  // Controlled_Buffer controlled_buffer_3
  assign controlled_buffer_1_out = and_1_out ? datain : 8'bz;  // Controlled_Buffer controlled_buffer_4
  and and_1 (and_1_out, timer_1_e, control_unit_1_ramen[1]);
  and and_2 (and_2_out, timer_1_e, control_unit_1_ramen[0]);
endmodule

module regfile (
  input  [7:0] in_1,
  input  [3:0] in_2,
  input  [1:0] in_3,
  input  [3:0] adb,
  input  [2:0] in_5,
  input  [3:0] pc,
  input  [1:0] sp,
  input  e16tr,
  output [7:0] out_9,
  output [15:0] out_10
);

  wire or_1_out;
  wire [1:0] demultiplexer_1_out0, demultiplexer_1_out1, demultiplexer_1_out2, demultiplexer_1_out3;
  wire [7:0] buffer_2_out, controlled_buffer_1_out, controlled_buffer_2_out, controlled_buffer_6_out,
       demultiplexer_2_out0, demultiplexer_2_out1, register_1_q, register_2_q, register_3_q, register_4_q,
       register_5_q, register_6_q, register_7_q, register_8_q, register_9_q, register_10_q;
  wire [15:0] counter_1_q, counter_2_q, register_11_q;

  or or_1 (or_1_out, in_2[2], in_5[2]);
  Demultiplexer #(.select(2), .width(2), .disabled(0), .enable("false")) demultiplexer_1 (
    .out0(demultiplexer_1_out0), .out1(demultiplexer_1_out1), .out2(demultiplexer_1_out2),
    .out3(demultiplexer_1_out3), .in(in_3), .sel(in_5[1:0]));
  Demultiplexer #(.width(8), .tristate("true"), .disabled(0), .enable("false")) demultiplexer_2 (
    .out0(demultiplexer_2_out0), .out1(demultiplexer_2_out1), .in(in_1), .sel(or_1_out));
  assign demultiplexer_2_out1 = controlled_buffer_1_out;  // Buffer buffer_1, 8 bits wide
  assign controlled_buffer_1_out = in_2[1] ? register_1_q : 8'bz;  // Controlled_Buffer controlled_buffer_1
  Register register_1 (.D(demultiplexer_2_out0), .Q(register_1_q), .clk(in_2[0]));  // open: en, clr
  assign controlled_buffer_2_out = demultiplexer_1_out0[1] ? register_2_q : 8'bz;  // Controlled_Buffer controlled_buffer_2
  Register register_2 (.D(demultiplexer_2_out0), .Q(register_2_q), .clk(demultiplexer_1_out0[0]));  // open: en, clr
  Register register_3 (.D(demultiplexer_2_out0), .Q(register_3_q), .clk(demultiplexer_1_out1[0]));  // open: en, clr
  assign controlled_buffer_2_out = demultiplexer_1_out1[1] ? register_3_q : 8'bz;  // Controlled_Buffer controlled_buffer_3
  assign controlled_buffer_2_out = demultiplexer_1_out2[1] ? register_4_q : 8'bz;  // Controlled_Buffer controlled_buffer_4
  Register register_4 (.D(demultiplexer_2_out0), .Q(register_4_q), .clk(demultiplexer_1_out2[0]));  // open: en, clr
  assign controlled_buffer_2_out = demultiplexer_1_out3[1] ? register_5_q : 8'bz;  // Controlled_Buffer controlled_buffer_5
  Register register_5 (.D(demultiplexer_2_out0), .Q(register_5_q), .clk(demultiplexer_1_out3[0]));  // open: en, clr
  Multiplexer #(.width(8), .disabled(0), .enable("false")) multiplexer_1 (
    .in0(controlled_buffer_2_out), .in1(buffer_2_out), .out(out_9), .sel(or_1_out));
  assign buffer_2_out = controlled_buffer_6_out;  // Buffer buffer_2, 8 bits wide
  assign controlled_buffer_6_out = in_2[1] ? register_6_q : 8'bz;  // Controlled_Buffer controlled_buffer_6
  Register register_6 (.D(demultiplexer_2_out1), .Q(register_6_q), .clk(in_2[0]));  // open: en, clr
  Register register_7 (.D(demultiplexer_2_out1), .Q(register_7_q), .clk(demultiplexer_1_out0[0]));  // open: en, clr
  assign buffer_2_out = demultiplexer_1_out0[1] ? register_7_q : 8'bz;  // Controlled_Buffer controlled_buffer_7
  assign buffer_2_out = demultiplexer_1_out1[1] ? register_8_q : 8'bz;  // Controlled_Buffer controlled_buffer_8
  Register register_8 (.D(demultiplexer_2_out1), .Q(register_8_q), .clk(demultiplexer_1_out1[0]));  // open: en, clr
  assign buffer_2_out = demultiplexer_1_out2[1] ? register_9_q : 8'bz;  // Controlled_Buffer controlled_buffer_9
  Register register_9 (.D(demultiplexer_2_out1), .Q(register_9_q), .clk(demultiplexer_1_out2[0]));  // open: en, clr
  Register register_10 (.D(demultiplexer_2_out1), .Q(register_10_q), .clk(demultiplexer_1_out3[0]));  // open: en, clr
  assign buffer_2_out = demultiplexer_1_out3[1] ? register_10_q : 8'bz;  // Controlled_Buffer controlled_buffer_10
  assign out_10 = in_2[3] ? {controlled_buffer_6_out, controlled_buffer_1_out} : 16'bz;  // Controlled_Buffer controlled_buffer_11
  assign out_10 = adb[3] ? counter_1_q : 16'bz;  // Controlled_Buffer controlled_buffer_12
  Counter #(.width(16), .max('hffff)) counter_1 (
    .load(adb[0]), .D({buffer_2_out, controlled_buffer_2_out}), .count(adb[1]), .Q(counter_1_q), .clk(adb[2]));  // open: carry, clr
  Counter #(.width(16), .max('hffff), .trigger("falling")) counter_2 (
    .load(pc[0]), .D({buffer_2_out, controlled_buffer_2_out}), .count(pc[1]), .Q(counter_2_q), .clk(pc[2]));  // open: carry, clr
  assign out_10 = pc[3] ? counter_2_q : 16'bz;  // Controlled_Buffer controlled_buffer_13
  Register #(.width(16)) register_11 (
    .D({buffer_2_out, controlled_buffer_2_out}), .Q(register_11_q), .clk(sp[0]));  // open: en, clr
  assign out_10 = sp[1] ? register_11_q : 16'bz;  // Controlled_Buffer controlled_buffer_14
  assign {demultiplexer_2_out1, demultiplexer_2_out0} = e16tr ? out_10 : 16'bz;  // Controlled_Buffer controlled_buffer_15
endmodule

module control_unit (
  input  s,
  input  [3:0] flg_in,
  input  [7:0] INST,
  input  [3:0] ct,
  input  e,
  output e16tr,
  output sBUS,
  output sIN,
  output [1:0] e_s_RAM,
  output [1:0] e_s_ACC,
  output sTMP,
  output eALU,
  output [1:0] e_s_FLG,
  output [2:0] OP,
  output sRST,
  output [3:0] e_s_ct_LD_ADB,
  output [3:0] e_s_ct_ld_PC,
  output [1:0] ramen,
  output [1:0] e_s_SP,
  output [3:0] hl_e_s_HL,
  output [2:0] REG,
  output [1:0] e_s_RA
);

  wire [9:9] flg_1_t_f;
  wire [19:19] controlled_buffer_2_out;
  wire [31:0] rom_1_data;

  FLG flg_1 (.in_1(flg_in), .t_f(flg_1_t_f[9]), .in_2(INST[1:0]));
  ROM #(.addrWidth(10), .dataWidth(32)) rom_1 (
    .addr({flg_1_t_f[9], INST[7:3], ct}),
    .data({rom_1_data[31:29], ramen[1], rom_1_data[27:10], ramen[0], rom_1_data[8:0]}));  // open: sel
  assign {sBUS, sIN, e_s_RAM[0], e_s_ACC[0], sTMP, e_s_FLG[0], sRST, e_s_ct_LD_ADB[2], e_s_ct_ld_PC[2], e_s_SP[0], hl_e_s_HL[0], e_s_RA[0]} = s ? {rom_1_data[11:10], ramen[0], rom_1_data[8:0]} : 12'bz;  // Controlled_Buffer controlled_buffer_1
  assign {controlled_buffer_2_out[19], e16tr, hl_e_s_HL[3], e_s_RAM[1], e_s_ACC[1], eALU, e_s_FLG[1], OP[0], OP[1], OP[2], e_s_ct_LD_ADB[0], e_s_ct_LD_ADB[1], e_s_ct_LD_ADB[3], e_s_ct_ld_PC[0], e_s_ct_ld_PC[1], e_s_ct_ld_PC[3], e_s_SP[1], hl_e_s_HL[2:1], e_s_RA[1]} = e ? {rom_1_data[31:29], ramen[1], rom_1_data[27:12]} : 20'bz;  // Controlled_Buffer controlled_buffer_2
  Pull_Resistor pull_resistor_1 (.node({sBUS, sIN, e_s_RAM[0], e_s_ACC[0], sTMP, e_s_FLG[0], sRST, e_s_ct_LD_ADB[2], e_s_ct_ld_PC[2], e_s_SP[0], hl_e_s_HL[0], e_s_RA[0]}));
  Pull_Resistor pull_resistor_2 (.node({controlled_buffer_2_out[19], e16tr, hl_e_s_HL[3], e_s_RAM[1], e_s_ACC[1], eALU, e_s_FLG[1], OP[0], OP[1], OP[2], e_s_ct_LD_ADB[0], e_s_ct_LD_ADB[1], e_s_ct_LD_ADB[3], e_s_ct_ld_PC[0], e_s_ct_ld_PC[1], e_s_ct_ld_PC[3], e_s_SP[1], hl_e_s_HL[2:1], e_s_RA[1]}));

  assign REG = INST[2:0];

  // Notes on the sheet:
  //   contents of rom_1 (hex, n*v repeats v):
  //   10030408 20 14*0 10030408 1100 20 13*0 10030408 8000001 20 13*0 10030408 10030009 20 13*0 10030408
  //   1003400a 1003000a 30002001 20 11*0 10030408 40008002 6100 10030088 5004042 2100 10030088 7000002
  //   30002001 20 6*0 10030408 1003400a 1003000a 20003200 20 11*0 10030408 40008002 6100 10030088 5004042
  //   2100 10030088 7000002 20003200 20
endmodule
