// Logisim project logv1.circ as structural Verilog: 7 circuits, main circuit motherboard
module motherboard (
);

  wire clock_1_out;
  wire [1:0] undriven_2;
  wire [7:0] ram_1_data;
  wire [15:0] undriven;

  CPU cpu_1 (.ClkIn(clock_1_out));  // open: in_1
  Clock clock_1 (.out(clock_1_out));
  // Probe on undriven
  // Probe on ram_1_data
  RAM #(.addrWidth(16)) ram_1 (
    .addr(undriven), .data(ram_1_data), .clk(undriven_2[1]), .ld(undriven_2[0]));  // open: sel, clr
  TTY tty_1 ();  // open: data, clk, we, clr
endmodule

module CPU (
  input  [7:0] in_1,
  input  ClkIn
);

  wire and_1_out, clock_1_out, decoder_1_out0, decoder_1_out1, decoder_1_out2, decoder_1_out3, not_1_out,
       or_1_out, t_ff_1_q;
  wire [1:0] regdec_1_out_4, regdec_1_out_4_2, regdec_1_out_4_3, regdec_1_out_4_4, regdec_1_out_4_5,
       regdec_1_out_4_6, regdec_1_out_4_7, regdec_1_out_4_8, t_ff_3_q;
  wire [3:0] alu_1_out_6, counter_1_q, register_2_q;
  wire [7:0] r0_q, r1_q, r2_q, r3_q, r4_q, r5_2_q, r5_q, r6_q, register_1_probe_lsb, register_1_probe_msb;
  wire [10:10] flg_1_t_f;
  wire [15:0] alu_1_out_5, BP_q, controlled_buffer_1_out, controlled_buffer_3_out, controlled_buffer_11_out,
       controlled_buffer_12_out, counter_2_q, multiplexer_1_out, multiplexer_2_out, register_3_q,
       register_4_q, register_5_q, register_6_q, shreg_1_out_3, shreg_2_out_3, SP_q;
  wire [31:0] rom_1_data;

  register register_1 (
    .probe_MSB(register_1_probe_msb), .probe_LSB(register_1_probe_lsb));  // open: _16_out, LSB_in, MSB_in, _16_out_2, LSB_out, MSB_out, Set, Enable
  // Probe on register_1_probe_msb
  // Probe on register_1_probe_lsb
  shreg shreg_1 (.in_1(controlled_buffer_1_out[7:0]), .in_2(controlled_buffer_11_out[9]), .out_3(shreg_1_out_3));
  not not_1 (not_1_out, clock_1_out);
  Clock clock_1 (.out(clock_1_out));
  Register r3 (.D(controlled_buffer_1_out[7:0]), .Q(r3_q), .clk(regdec_1_out_4_4[1]));  // open: en, clr
  assign controlled_buffer_1_out[7:0] = regdec_1_out_4_4[0] ? r3_q : 8'bz;  // Controlled_Buffer controlled_buffer_1
  assign controlled_buffer_1_out[7:0] = regdec_1_out_4_8[0] ? r5_q : 8'bz;  // Controlled_Buffer controlled_buffer_2
  Register r5 (.D(controlled_buffer_1_out[7:0]), .Q(r5_q), .clk(regdec_1_out_4_8[1]));  // open: en, clr
  Register #(.width(4)) register_2 (
    .D(alu_1_out_6), .Q(register_2_q), .clk(controlled_buffer_11_out[8]));  // open: en, clr
  Register #(.width(16)) register_3 (
    .D(shreg_1_out_3), .Q(register_3_q), .clk(controlled_buffer_11_out[11]));  // open: en, clr
  // Probe on register_3_q[15:10]
  and and_1 (and_1_out, t_ff_1_q, decoder_1_out0);
  T_Flip_Flop t_ff_1 (
    .clk(controlled_buffer_11_out[10]), .T(controlled_buffer_11_out[10]), .Q(t_ff_1_q), .reset(decoder_1_out1));  // open: Qn, preset, en
  T_Flip_Flop t_ff_2 (.clk(not_1_out), .T(not_1_out), .Q(t_ff_3_q[1]));  // open: Qn, preset, reset, en
  T_Flip_Flop t_ff_3 (.clk(clock_1_out), .T(clock_1_out), .Q(t_ff_3_q[0]));  // open: Qn, preset, reset, en
  Register #(.width(16)) BP (
    .D(controlled_buffer_3_out), .Q(BP_q), .clk(controlled_buffer_11_out[6]));  // open: en, clr
  assign controlled_buffer_3_out = controlled_buffer_12_out[9] ? BP_q : 16'bz;  // Controlled_Buffer controlled_buffer_3
  Register r2 (.D(controlled_buffer_1_out[7:0]), .Q(r2_q), .clk(regdec_1_out_4_3[1]));  // open: en, clr
  assign controlled_buffer_1_out[7:0] = regdec_1_out_4_3[0] ? r2_q : 8'bz;  // Controlled_Buffer controlled_buffer_4
  Register r6 (.D(controlled_buffer_1_out[7:0]), .Q(r6_q), .clk(regdec_1_out_4_7[1]));  // open: en, clr
  assign controlled_buffer_1_out[7:0] = regdec_1_out_4_7[0] ? r6_q : 8'bz;  // Controlled_Buffer controlled_buffer_5
  FLG flg_1 (.in_1(register_2_q), .cgez(register_3_q[9:6]), .t_f(flg_1_t_f[10]));
  Counter #(.width(4), .max('hf)) counter_1 (
    .Q(counter_1_q), .clk(decoder_1_out0), .clr(and_1_out));  // open: load, D, count, carry
  Decoder #(.select(2), .disabled(0), .enable("false")) decoder_1 (
    .out0(decoder_1_out0), .out1(decoder_1_out1), .out2(decoder_1_out2), .out3(decoder_1_out3), .sel(t_ff_3_q));
  Register r1 (.D(controlled_buffer_1_out[7:0]), .Q(r1_q), .clk(regdec_1_out_4_2[1]));  // open: en, clr
  assign controlled_buffer_1_out[7:0] = regdec_1_out_4_2[0] ? r1_q : 8'bz;  // Controlled_Buffer controlled_buffer_6
  Register r5_2 (.D(controlled_buffer_1_out[7:0]), .Q(r5_2_q), .clk(regdec_1_out_4_6[1]));  // open: en, clr
  assign controlled_buffer_1_out[7:0] = regdec_1_out_4_6[0] ? r5_2_q : 8'bz;  // Controlled_Buffer controlled_buffer_7
  or or_1 (or_1_out, decoder_1_out1, decoder_1_out2, decoder_1_out3);
  Register #(.width(16)) SP (
    .D(controlled_buffer_3_out), .Q(SP_q), .clk(controlled_buffer_11_out[5]));  // open: en, clr
  assign controlled_buffer_3_out = controlled_buffer_12_out[8] ? SP_q : 16'bz;  // Controlled_Buffer controlled_buffer_8
  assign controlled_buffer_1_out[7:0] = regdec_1_out_4[0] ? r0_q : 8'bz;  // Controlled_Buffer controlled_buffer_9
  Register r0 (.D(controlled_buffer_1_out[7:0]), .Q(r0_q), .clk(regdec_1_out_4[1]));  // open: en, clr
  assign controlled_buffer_1_out[7:0] = regdec_1_out_4_5[0] ? r4_q : 8'bz;  // Controlled_Buffer controlled_buffer_10
  Register r4 (.D(controlled_buffer_1_out[7:0]), .Q(r4_q), .clk(regdec_1_out_4_5[1]));  // open: en, clr
  ROM #(.addrWidth(11), .dataWidth(32)) rom_1 (
    .addr({flg_1_t_f[10], register_3_q[15:10], counter_1_q}), .data(rom_1_data));  // open: sel
  // Probe on controlled_buffer_3_out
  regdec regdec_1 (
    .out_4({regdec_1_out_4_8, regdec_1_out_4_7, regdec_1_out_4_6, regdec_1_out_4_5, regdec_1_out_4_4, regdec_1_out_4_3, regdec_1_out_4_2, regdec_1_out_4}),
    .EA_EB(controlled_buffer_11_out[13:12]), .EA_EB_2(controlled_buffer_12_out[11:10]),
    .in_1(register_3_q[5:0]));
  // Probe on register_3_q[5:0]
  assign controlled_buffer_11_out = decoder_1_out3 ? rom_1_data[15:0] : 16'bz;  // Controlled_Buffer controlled_buffer_11
  Pull_Resistor pull_resistor_1 (.node(controlled_buffer_11_out));
  assign controlled_buffer_12_out = or_1_out ? rom_1_data[31:16] : 16'bz;  // Controlled_Buffer controlled_buffer_12
  Pull_Resistor pull_resistor_2 (.node(controlled_buffer_12_out));
  // Probe on in_1
  shreg shreg_2 (.in_1(controlled_buffer_1_out[7:0]), .in_2(controlled_buffer_11_out[4]), .out_3(shreg_2_out_3));
  Counter #(.width(16), .max('hffff)) counter_2 (
    .load(controlled_buffer_12_out[5]), .D(shreg_2_out_3), .count(controlled_buffer_12_out[4]),
    .Q(counter_2_q), .clk(controlled_buffer_11_out[3]));  // open: carry, clr
  assign controlled_buffer_3_out = controlled_buffer_12_out[3] ? counter_2_q : 16'bz;  // Controlled_Buffer controlled_buffer_13
  // Probe on controlled_buffer_1_out[7:0]
  Register #(.width(16)) register_4 (
    .D(controlled_buffer_3_out), .Q(register_4_q), .clk(controlled_buffer_11_out[2]));  // open: en, clr
  Multiplexer #(.width(16), .disabled(0), .enable("false")) multiplexer_1 (
    .in0({{8{1'b0}}, controlled_buffer_1_out[7:0]}), .in1(controlled_buffer_3_out), .out(multiplexer_1_out),
    .sel(controlled_buffer_12_out[7]));
  Multiplexer #(.width(16), .disabled(0), .enable("false")) multiplexer_2 (
    .in0({{8{1'b0}}, controlled_buffer_1_out[7:0]}), .in1(controlled_buffer_3_out), .out(multiplexer_2_out),
    .sel(controlled_buffer_12_out[7]));
  ALU alu_1 (
    .A(multiplexer_2_out), .B(register_5_q), .out_6(alu_1_out_6), .in_4(controlled_buffer_12_out[2:1]),
    .out_5(alu_1_out_5));  // open: in_3
  // Probe on controlled_buffer_1_out[7:0]
  Register #(.width(16)) register_5 (
    .D(multiplexer_1_out), .Q(register_5_q), .clk(controlled_buffer_11_out[1]));  // open: en, clr
  RAM #(.addrWidth(16)) ram_1 (
    .addr(register_4_q), .data(controlled_buffer_1_out[7:0]), .clk(controlled_buffer_11_out[7]),
    .ld(controlled_buffer_12_out[6]));  // open: sel, clr
  Register #(.width(16)) register_6 (
    .D(alu_1_out_5), .Q(register_6_q), .clk(controlled_buffer_11_out[0]));  // open: en, clr
  Demultiplexer #(.width(16)) demultiplexer_1 (
    .out0(controlled_buffer_1_out), .out1(controlled_buffer_3_out), .in(register_6_q),
    .sel(controlled_buffer_12_out[7]), .en(controlled_buffer_12_out[0]));

  // Notes on the sheet:
  //   contents of rom_1 (hex, n*v repeats v):
  //   80004 500208 80004 500208 800 400 10*0 80004 500208 80004 500208 800 80004 501008 400 8*0 80004
  //   500208 80004 500208 800 80004 d0000a 1800001 810004 4000080 400 5*0 80004 500208 80004 500208 800
  //   80004 d0000a 1800001 810004 401000 400 5*0 80004 500208 80004 500208 800 8000002 4000001 12000 400
  //   7*0 80004 500208 80004 500208 800 8000002 4020001 12000 400 7*0 80004 500208 80004 500208 800
  //   8000002 4040001 12000 400 7*0 80004 500208 80004 500208 800 8000002 4060100 400 8*0 80004 500208
  //   80004 500208 800 80004 500018 80004 500018 200008 400 5*0 80004 500208 80004 500208 800 400 10*0
  //   80004 500208 80004 500208 800 400 10*0 80004 500208 80004 500208 800 400 10*0 80004 500208 80004
  //   500208 800 400 10*0 80004 500208 80004 500208 800 400 10*0 80004 500208 80004 500208 800 400 10*0
  //   80004 500208 80004 500208 800 400 10*0 80004 500208 80004 500208 800 400 10*0 80004 500208 80004
  //   500208 800 400 10*0 80004 500208 80004 500208 800 400 10*0 80004 500208 80004 500208 800 400 10*0
  //   80004 500208 80004 500208 800 400 10*0 80004 500208 80004 500208 800 400 10*0 80004 500208 80004
  //   500208 800 400 10*0 80004 500208 80004 500208 800 400 10*0 80004 500208 80004 500208 800 400 10*0
  //   80004 500208 80004 500208 800 400 10*0 80004 500208 80004 500208 800 400 10*0 80004 500208 80004
  //   500208 800 400 10*0 80004 500208 80004 500208 800 400 10*0 80004 500208 80004 500208 800 400 10*0
  //   80004 500208 80004 500208 800 400 10*0 80004 500208 80004 500208 800 400 10*0 80004 500208 80004
  //   500208 800 400 10*0 80004 500208 80004 500208 800 400 10*0 80004 500208 80004 500208 800 400 10*0
  //   80004 500208 80004 500208 800 400 10*0 80004 500208 80004 500208 800 400 10*0 80004 500208 80004
  //   500208 800 400 10*0 80004 500208 80004 500208 800 400 10*0 80004 500208 80004 500208 800 400 10*0
  //   80004 500208 80004 500208 800 400 10*0 80004 500208 80004 500208 800 400 10*0 80004 500208 80004
  //   500208 800 400 10*0 80004 500208 80004 500208 800 400 10*0 80004 500208 80004 500208 800 400 10*0
  //   80004 500208 80004 500208 800 400 10*0 80004 500208 80004 500208 800 400 10*0 80004 500208 80004
  //   500208 800 400 10*0 80004 500208 80004 500208 800 400 10*0 80004 500208 80004 500208 800 400 10*0
  //   80004 500208 80004 500208 800 400 10*0 80004 500208 80004 500208 800 400 10*0 80004 500208 80004
  //   500208 800 400 10*0 80004 500208 80004 500208 800 400 10*0 80004 500208 80004 500208 800 400 10*0
  //   80004 500208 80004 500208 800 400 10*0 80004 500208 80004 500208 800 400 10*0 80004 500208 80004
  //   500208 800 400 10*0 80004 500208 80004 500208 800 400 10*0 80004 500208 80004 500208 800 400 10*0
  //   80004 500208 80004 500208 800 400 10*0 80004 500208 80004 500208 800 400 10*0 80004 500208 80004
  //   500208 800 400 10*0 80004 500208 80004 500208 800 400 10*0 80004 500208 80004 500208 800 400 10*0
  //   80004 500208 80004 500208 800 80004 501008 400 8*0 80004 500208 80004 500208 800 80004 d0000a
  //   1800001 810004 4000080 400 5*0 80004 500208 80004 500208 800 80004 d0000a 1800001 810004 401000 400
  //   5*0 80004 500208 80004 500208 800 8000002 4000001 12000 400 7*0 80004 500208 80004 500208 800
  //   8000002 4020001 12000 400 7*0 80004 500208 80004 500208 800 8000002 4040001 12000 400 7*0 80004
  //   500208 80004 500208 800 8000002 4060100 400 8*0 80004 500208 80004 500208 800 80004 500018 80004
  //   500018 200008 400 5*0 80004 500208 80004 500208 800 80004 500018 80004 500018 200008 400 5*0 80004
  //   500208 80004 500208 800 400 10*0 80004 500208 80004 500208 800 400 10*0 80004 500208 80004 500208
  //   800 400 10*0 80004 500208 80004 500208 800 400 10*0 80004 500208 80004 500208 800 400 10*0 80004
  //   500208 80004 500208 800 400 10*0 80004 500208 80004 500208 800 400 10*0 80004 500208 80004 500208
  //   800 400 10*0 80004 500208 80004 500208 800 400 10*0 80004 500208 80004 500208 800 400 10*0 80004
  //   500208 80004 500208 800 400 10*0 80004 500208 80004 500208 800 400 10*0 80004 500208 80004 500208
  //   800 400 10*0 80004 500208 80004 500208 800 400 10*0 80004 500208 80004 500208 800 400 10*0 80004
  //   500208 80004 500208 800 400 10*0 80004 500208 80004 500208 800 400 10*0 80004 500208 80004 500208
  //   800 400 10*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
endmodule

module shreg (
  input  [7:0] in_1,
  input  in_2,
  output [15:0] out_3
);

  Register register_1 (.D(in_1), .Q(out_3[7:0]), .clk(in_2));  // open: en, clr
  Register register_2 (.D(out_3[7:0]), .Q(out_3[15:8]), .clk(in_2));  // open: en, clr
endmodule

module regdec (
  input  [5:0] in_1,
  input  [1:0] EA_EB,
  input  [1:0] EA_EB_2,
  output [15:0] out_4
);

  wire [1:0] demultiplexer_1_out0, demultiplexer_1_out1, demultiplexer_1_out2, demultiplexer_1_out3,
       demultiplexer_1_out4, demultiplexer_1_out5, demultiplexer_1_out6, demultiplexer_1_out7,
       demultiplexer_2_out0, demultiplexer_2_out1, demultiplexer_2_out2, demultiplexer_2_out3,
       demultiplexer_2_out4, demultiplexer_2_out5, demultiplexer_2_out6, demultiplexer_2_out7;

  assign out_4[1:0] = demultiplexer_1_out0 | demultiplexer_2_out0;  // OR_Gate or_1, 2 bits wide
  assign out_4[3:2] = demultiplexer_1_out1 | demultiplexer_2_out1;  // OR_Gate or_2, 2 bits wide
  assign out_4[5:4] = demultiplexer_1_out2 | demultiplexer_2_out2;  // OR_Gate or_3, 2 bits wide
  assign out_4[7:6] = demultiplexer_1_out3 | demultiplexer_2_out3;  // OR_Gate or_4, 2 bits wide
  assign out_4[9:8] = demultiplexer_1_out4 | demultiplexer_2_out4;  // OR_Gate or_5, 2 bits wide
  assign out_4[11:10] = demultiplexer_1_out5 | demultiplexer_2_out5;  // OR_Gate or_6, 2 bits wide
  assign out_4[13:12] = demultiplexer_1_out6 | demultiplexer_2_out6;  // OR_Gate or_7, 2 bits wide
  assign out_4[15:14] = demultiplexer_1_out7 | demultiplexer_2_out7;  // OR_Gate or_8, 2 bits wide
  Demultiplexer #(.select(3), .width(2), .disabled(0), .enable("false")) demultiplexer_1 (
    .out0(demultiplexer_1_out0), .out1(demultiplexer_1_out1), .out2(demultiplexer_1_out2),
    .out3(demultiplexer_1_out3), .out4(demultiplexer_1_out4), .out5(demultiplexer_1_out5),
    .out6(demultiplexer_1_out6), .out7(demultiplexer_1_out7), .in({EA_EB[1], EA_EB_2[1]}), .sel(in_1[5:3]));
  // Probe on in_1[5:3]
  // Probe on in_1[2:0]
  Demultiplexer #(.select(3), .width(2), .disabled(0), .enable("false")) demultiplexer_2 (
    .out0(demultiplexer_2_out0), .out1(demultiplexer_2_out1), .out2(demultiplexer_2_out2),
    .out3(demultiplexer_2_out3), .out4(demultiplexer_2_out4), .out5(demultiplexer_2_out5),
    .out6(demultiplexer_2_out6), .out7(demultiplexer_2_out7), .in({EA_EB[0], EA_EB_2[0]}), .sel(in_1[2:0]));
endmodule

module ALU (
  input  [15:0] A,
  input  [15:0] B,
  input  in_3,
  input  [1:0] in_4,
  output [15:0] out_5,
  output [3:0] out_6
);

  wire [15:0] adder_1_out, and_1_out, not_1_out;

  Pull_Resistor pull_resistor_1 (.node(A));
  Pull_Resistor pull_resistor_2 (.node(B));
  Adder #(.width(16)) adder_1 (.a(A), .b(B), .out(adder_1_out), .cin(in_3), .cout(out_6[3]));
  assign and_1_out = A & B;  // AND_Gate and_1, 16 bits wide
  assign not_1_out = ~A;  // NOT_Gate not_1, 16 bits wide
  Comparator #(.width(16)) comparator_1 (.a(A), .b(B), .gt(out_6[2]), .eq(out_6[1]));  // open: lt
  or or_1 (out_6[0], A[0], A[1], A[2], A[3], A[4], A[5], A[6], A[7], A[8], A[9], A[10], A[11], A[12], A[13], A[14], A[15]);
  Pull_Resistor pull_resistor_3 (.node(out_6));
  Multiplexer #(.select(2), .width(16), .disabled(0), .enable("false")) multiplexer_1 (
    .in0(adder_1_out), .in1(and_1_out), .in2(not_1_out), .out(out_5), .sel(in_4));  // open: in3
endmodule

module FLG (
  input  [3:0] in_1,
  input  [3:0] cgez,
  output t_f
);

  wire [3:0] and_1_out;

  // Probe on and_1_out
  assign and_1_out = in_1 & cgez;  // AND_Gate and_1, 4 bits wide
  or or_1 (t_f, and_1_out[0], and_1_out[1], and_1_out[2], and_1_out[3]);
endmodule

module register (
  input  [15:0] _16_out,
  input  [7:0] LSB_in,
  input  [7:0] MSB_in,
  input  [1:0] Set,
  input  [1:0] Enable,
  output [7:0] probe_MSB,
  output [7:0] probe_LSB,
  output [15:0] _16_out_2,
  output [7:0] LSB_out,
  output [7:0] MSB_out
);

  wire decoder_1_out1, decoder_1_out2, decoder_1_out3, or_1_out, or_2_out;
  wire [7:0] demultiplexer_1_out3, undriven, undriven_2;
  wire [15:0] multiplexer_1_out;
  wire [15:8] demultiplexer_1_out2;

  Multiplexer #(.select(2), .width(16), .disabled(0), .enable("false")) multiplexer_1 (
    .in1(_16_out), .in2({undriven, LSB_in}), .in3({MSB_in, undriven_2}), .out(multiplexer_1_out), .sel(Set));  // open: in0
  Decoder #(.select(2), .disabled(0), .enable("false")) decoder_1 (
    .out1(decoder_1_out1), .out2(decoder_1_out2), .out3(decoder_1_out3), .sel(Set));  // open: out0
  Demultiplexer #(.select(2), .width(16), .tristate("true"), .enable("false")) demultiplexer_1 (
    .out1(_16_out_2), .out2({demultiplexer_1_out2, LSB_out}), .out3({MSB_out, demultiplexer_1_out3}),
    .in({probe_MSB, probe_LSB}), .sel(Enable));  // open: out0
  Register register_1 (.D(multiplexer_1_out[15:8]), .Q(probe_MSB), .clk(or_1_out));  // open: en, clr
  or or_1 (or_1_out, decoder_1_out1, decoder_1_out3);
  Register register_2 (.D(multiplexer_1_out[7:0]), .Q(probe_LSB), .clk(or_2_out));  // open: en, clr
  or or_2 (or_2_out, decoder_1_out1, decoder_1_out2);
endmodule
