// Logisim project logv2.circ as structural Verilog: 7 circuits, main circuit motherboard
module motherboard (
);

  wire cpu_1_p1;
  wire [1:0] cpu_1_p3;
  wire [7:0] cpu_1_p4;
  wire [15:0] cpu_1_p2;

  // CPU cpu_1: pin names not known; wires that end beside it: cpu_1_p1, cpu_1_p2, cpu_1_p3, cpu_1_p4
  Clock clock_1 (.out(cpu_1_p1));
  // Probe on cpu_1_p2
  // Probe on cpu_1_p4
  RAM #(.addrWidth(16)) ram_1 (
    .addr(cpu_1_p2), .data(cpu_1_p4), .clk(cpu_1_p3[1]), .ld(cpu_1_p3[0]));  // open: sel, clr
  TTY tty_1 ();  // open: data, clk, we, clr
endmodule

module CPU (
  input  in_1,
  input  [1:0] in_2,
  input  [3:0] in_3,
  input  [1:0] in_4,
  input  [1:0] in_5,
  input  [5:0] in_6,
  input  [2:0] in_7,
  input  [7:0] in_8,
  input  ClkIn
);

  wire and_1_out, clock_1_out, decoder_1_out0, decoder_1_out1, decoder_1_out2, decoder_1_out3, not_1_out,
       or_1_out, t_ff_1_q, undriven_2, undriven_3, undriven_4, undriven_5, undriven_6, undriven_7,
       undriven_8, undriven_9;
  wire [1:0] regdec_1_out_4, regdec_1_out_4_2, regdec_1_out_4_3, regdec_1_out_4_4, regdec_1_out_4_5,
       regdec_1_out_4_6, regdec_1_out_4_7, regdec_1_out_4_8, t_ff_3_q;
  wire [2:0] undriven_10, undriven_11;
  wire [3:0] counter_1_q, register_3_q, undriven;
  wire [7:0] controlled_buffer_2_out, register_2_q, register_6_q, register_8_q, register_10_q;
  wire [10:10] flg_1_t_f;
  wire [15:0] alu_1_out, controlled_buffer_1_out, counter_2_q, n16_1_reg_1__16_out, pull_resistor_1_node,
       pull_resistor_2_node, register_1_q, register_4_q, register_5_q, register_7_q, register_9_q,
       register_11_q;
  wire [31:0] rom_1_data;

  not not_1 (not_1_out, clock_1_out);
  Clock clock_1 (.out(clock_1_out));
  assign controlled_buffer_1_out = regdec_1_out_4_8[0] ? register_1_q : 16'bz;  // Controlled_Buffer controlled_buffer_1
  Register #(.width(16)) register_1 (
    .D(controlled_buffer_1_out), .Q(register_1_q), .clk(regdec_1_out_4_8[1]), .clr(undriven_2));  // open: en
  assign controlled_buffer_2_out = regdec_1_out_4_4[0] ? register_2_q : 8'bz;  // Controlled_Buffer controlled_buffer_2
  Register register_2 (
    .D(controlled_buffer_2_out), .Q(register_2_q), .clk(regdec_1_out_4_4[1]), .clr(undriven_3));  // open: en
  // Probe on controlled_buffer_2_out
  Register #(.width(4)) register_3 (.D(undriven), .Q(register_3_q), .clk(pull_resistor_1_node[8]));  // open: en, clr
  Register #(.width(16)) register_4 (
    .D(controlled_buffer_1_out), .Q(register_4_q), .clk(pull_resistor_1_node[11]));  // open: en, clr
  // Probe on register_4_q[15:10]
  and and_1 (and_1_out, t_ff_1_q, decoder_1_out0);
  T_Flip_Flop t_ff_1 (
    .clk(pull_resistor_1_node[10]), .T(pull_resistor_1_node[10]), .Q(t_ff_1_q), .reset(decoder_1_out1));  // open: Qn, preset, en
  T_Flip_Flop t_ff_2 (.clk(not_1_out), .T(not_1_out), .Q(t_ff_3_q[1]));  // open: Qn, preset, reset, en
  T_Flip_Flop t_ff_3 (.clk(clock_1_out), .T(clock_1_out), .Q(t_ff_3_q[0]));  // open: Qn, preset, reset, en
  Register #(.width(16)) register_5 (
    .D(controlled_buffer_1_out), .Q(register_5_q), .clk(regdec_1_out_4_7[1]), .clr(undriven_4));  // open: en
  assign controlled_buffer_1_out = regdec_1_out_4_7[0] ? register_5_q : 16'bz;  // Controlled_Buffer controlled_buffer_3
  Register register_6 (
    .D(controlled_buffer_2_out), .Q(register_6_q), .clk(regdec_1_out_4_3[1]), .clr(undriven_5));  // open: en
  assign controlled_buffer_2_out = regdec_1_out_4_3[0] ? register_6_q : 8'bz;  // Controlled_Buffer controlled_buffer_4
  FLG flg_1 (.in_1(register_3_q), .cgez(register_4_q[9:6]), .t_f(flg_1_t_f[10]));
  Counter #(.width(4), .max('hf)) counter_1 (
    .Q(counter_1_q), .clk(decoder_1_out0), .clr(and_1_out));  // open: load, D, count, carry
  Decoder #(.select(2), .disabled(0), .enable("false")) decoder_1 (
    .out0(decoder_1_out0), .out1(decoder_1_out1), .out2(decoder_1_out2), .out3(decoder_1_out3), .sel(t_ff_3_q));
  Register #(.width(16)) register_7 (
    .D(controlled_buffer_1_out), .Q(register_7_q), .clk(regdec_1_out_4_6[1]), .clr(undriven_6));  // open: en
  assign controlled_buffer_1_out = regdec_1_out_4_6[0] ? register_7_q : 16'bz;  // Controlled_Buffer controlled_buffer_5
  assign controlled_buffer_2_out = regdec_1_out_4_2[0] ? register_8_q : 8'bz;  // Controlled_Buffer controlled_buffer_6
  Register register_8 (
    .D(controlled_buffer_2_out), .Q(register_8_q), .clk(regdec_1_out_4_2[1]), .clr(undriven_7));  // open: en
  or or_1 (or_1_out, decoder_1_out1, decoder_1_out2, decoder_1_out3);
  Register #(.width(16)) register_9 (
    .D(controlled_buffer_1_out), .Q(register_9_q), .clk(regdec_1_out_4_5[1]), .clr(undriven_8));  // open: en
  assign controlled_buffer_1_out = regdec_1_out_4_5[0] ? register_9_q : 16'bz;  // Controlled_Buffer controlled_buffer_7
  assign controlled_buffer_2_out = regdec_1_out_4[0] ? register_10_q : 8'bz;  // Controlled_Buffer controlled_buffer_8
  Register register_10 (
    .D(controlled_buffer_2_out), .Q(register_10_q), .clk(regdec_1_out_4[1]), .clr(undriven_9));  // open: en
  ROM #(.addrWidth(11), .dataWidth(32)) rom_1 (
    .addr({flg_1_t_f[10], register_4_q[15:10], counter_1_q}), .data(rom_1_data));  // open: sel
  regdec regdec_1 (
    .EA_EB(in_5), .EA_EB_2(in_4), .in_1(in_6),
    .out_4({regdec_1_out_4_8, regdec_1_out_4_7, regdec_1_out_4_6, regdec_1_out_4_5, regdec_1_out_4_4, regdec_1_out_4_3, regdec_1_out_4_2, regdec_1_out_4}));
  // Probe on register_4_q[5:0]
  Pull_Resistor pull_resistor_1 (.node(pull_resistor_1_node));
  assign pull_resistor_1_node = decoder_1_out3 ? rom_1_data[15:0] : 16'bz;  // Controlled_Buffer controlled_buffer_9
  Pull_Resistor pull_resistor_2 (.node(pull_resistor_2_node));
  assign pull_resistor_2_node = or_1_out ? rom_1_data[31:16] : 16'bz;  // Controlled_Buffer controlled_buffer_10
  // Probe on in_8
  shreg shreg_1 (
    ._16_in(controlled_buffer_1_out), ._8_in(controlled_buffer_2_out), .sSH(in_7[0]), .e16SH(in_7[2]),
    .eSH(in_7[1]), ._8_out(controlled_buffer_2_out), ._16_out(controlled_buffer_1_out));
  assign controlled_buffer_1_out = in_3[0] ? counter_2_q : 16'bz;  // Controlled_Buffer controlled_buffer_11
  Counter #(.width(16), .max('hffff)) counter_2 (
    .load(in_3[3]), .D(controlled_buffer_1_out), .count(in_3[2]), .Q(counter_2_q), .clk(in_3[1]));  // open: carry, clr
  // Probe on controlled_buffer_1_out
  Register #(.width(16)) register_11 (.D(controlled_buffer_1_out), .Q(register_11_q), .clk(in_1));  // open: en, clr
  ALU alu_1 (
    .A(controlled_buffer_1_out), .B(n16_1_reg_1__16_out), .out(alu_1_out), .A_8(controlled_buffer_2_out));  // open: Carry_in, C_G_E_Z, _16, OP
  _16_1_reg u_16_1_reg_1 (
    ._16_S_E(undriven_11), ._16_in(controlled_buffer_1_out), ._8_in(controlled_buffer_2_out),
    ._16_out(n16_1_reg_1__16_out));  // open: _8_out
  _16_1_reg u_16_1_reg_2 (
    ._16_S_E(undriven_10), ._16_in(alu_1_out), ._8_out(controlled_buffer_2_out),
    ._16_out(controlled_buffer_1_out));  // open: _8_in
  RAM #(.addrWidth(16)) ram_1 (
    .addr(register_11_q), .data(controlled_buffer_2_out), .clk(in_2[1]), .ld(in_2[0]));  // open: sel, clr

  // Notes on the sheet:
  //   contents of rom_1 (hex, n*v repeats v):
  //   80004 500208 80004 500208 800 400 10*0 80004 500208 80004 500208 800 80004 501008 400 8*0 80004
  //   500208 80004 500208 800 80004 d0000a 1800001 810004 4000080 400 5*0 80004 500208 80004 500208 800
  //   80004 d0000a 1800001 810004 401000 400 5*0 80004 500208 80004 500208 800 8000002 4000001 12000 400
  //   7*0 80004 500208 80004 500208 800 8000002 4020001 12000 400 7*0 80004 500208 80004 500208 800
  //   8000002 4040001 12000 400 7*0 80004 500208 80004 500208 800 8000002 4060100 400 8*0 80004 500208
  //   80004 500208 800 80004 500018 80004 500018 200008 400 5*0 80004 500208 80004 500208 800 400 10*0
  //   80004 500208 80004 500208 800 400 10*0 80004 500208 80004 500208 800 400 10*0 80004 500208 80004
  //   500208 800 400 10*0 80004 500208 80004 500208 800 400 10*0 80004 500208 80004 500208 800 400 10*0
  //   80004 500208 80004 500208 800 400 10*0 80004 500208 80004 500208 800 400 10*0 80004 500208 80004
  //   500208 800 400 10*0 80004 500208 80004 500208 800 400 10*0 80004 500208 80004 500208 800 400 10*0
  //   80004 500208 80004 500208 800 400 10*0 80004 500208 80004 500208 800 400 10*0 80004 500208 80004
  //   500208 800 400 10*0 80004 500208 80004 500208 800 400 10*0 80004 500208 80004 500208 800 400 10*0
  //   80004 500208 80004 500208 800 400 10*0 80004 500208 80004 500208 800 400 10*0 80004 500208 80004
  //   500208 800 400 10*0 80004 500208 80004 500208 800 400 10*0 80004 500208 80004 500208 800 400 10*0
  //   80004 500208 80004 500208 800 400 10*0 80004 500208 80004 500208 800 400 10*0 80004 500208 80004
  //   500208 800 400 10*0 80004 500208 80004 500208 800 400 10*0 80004 500208 80004 500208 800 400 10*0
  //   80004 500208 80004 500208 800 400 10*0 80004 500208 80004 500208 800 400 10*0 80004 500208 80004
  //   500208 800 400 10*0 80004 500208 80004 500208 800 400 10*0 80004 500208 80004 500208 800 400 10*0
  //   80004 500208 80004 500208 800 400 10*0 80004 500208 80004 500208 800 400 10*0 80004 500208 80004
  //   500208 800 400 10*0 80004 500208 80004 500208 800 400 10*0 80004 500208 80004 500208 800 400 10*0
  //   80004 500208 80004 500208 800 400 10*0 80004 500208 80004 500208 800 400 10*0 80004 500208 80004
  //   500208 800 400 10*0 80004 500208 80004 500208 800 400 10*0 80004 500208 80004 500208 800 400 10*0
  //   80004 500208 80004 500208 800 400 10*0 80004 500208 80004 500208 800 400 10*0 80004 500208 80004
  //   500208 800 400 10*0 80004 500208 80004 500208 800 400 10*0 80004 500208 80004 500208 800 400 10*0
  //   80004 500208 80004 500208 800 400 10*0 80004 500208 80004 500208 800 400 10*0 80004 500208 80004
  //   500208 800 400 10*0 80004 500208 80004 500208 800 400 10*0 80004 500208 80004 500208 800 400 10*0
  //   80004 500208 80004 500208 800 400 10*0 80004 500208 80004 500208 800 400 10*0 80004 500208 80004
  //   500208 800 400 10*0 80004 500208 80004 500208 800 400 10*0 80004 500208 80004 500208 800 400 10*0
  //   80004 500208 80004 500208 800 80004 501008 400 8*0 80004 500208 80004 500208 800 80004 d0000a
  //   1800001 810004 4000080 400 5*0 80004 500208 80004 500208 800 80004 d0000a 1800001 810004 401000 400
  //   5*0 80004 500208 80004 500208 800 8000002 4000001 12000 400 7*0 80004 500208 80004 500208 800
  //   8000002 4020001 12000 400 7*0 80004 500208 80004 500208 800 8000002 4040001 12000 400 7*0 80004
  //   500208 80004 500208 800 8000002 4060100 400 8*0 80004 500208 80004 500208 800 80004 500018 80004
  //   500018 200008 400 5*0 80004 500208 80004 500208 800 80004 500018 80004 500018 200008 400 5*0 80004
  //   500208 80004 500208 800 400 10*0 80004 500208 80004 500208 800 400 10*0 80004 500208 80004 500208
  //   800 400 10*0 80004 500208 80004 500208 800 400 10*0 80004 500208 80004 500208 800 400 10*0 80004
  //   500208 80004 500208 800 400 10*0 80004 500208 80004 500208 800 400 10*0 80004 500208 80004 500208
  //   800 400 10*0 80004 500208 80004 500208 800 400 10*0 80004 500208 80004 500208 800 400 10*0 80004
  //   500208 80004 500208 800 400 10*0 80004 500208 80004 500208 800 400 10*0 80004 500208 80004 500208
  //   800 400 10*0 80004 500208 80004 500208 800 400 10*0 80004 500208 80004 500208 800 400 10*0 80004
  //   500208 80004 500208 800 400 10*0 80004 500208 80004 500208 800 400 10*0 80004 500208 80004 500208
  //   800 400 10*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
endmodule

module shreg (
  input  e16SH,
  input  eSH,
  input  [15:0] _16_in,
  input  [7:0] _8_in,
  input  sSH,
  output [7:0] _8_out,
  output [15:0] _16_out
);

  wire and_1_out, or_1_out;
  wire [7:0] shift_register_1_q0, shift_register_1_q1;

  // Probe on _16_in
  // Probe on _8_in
  Shift_Register #(.width(8), .length(2), .trigger("falling")) shift_register_1 (
    .shift(1'b1), .in(_8_in), .clk(or_1_out), .load(e16SH), .d0(_16_in[15:8]), .q0(shift_register_1_q0),
    .d1(_16_in[7:0]), .q1(shift_register_1_q1));  // open: out, clr
  or or_1 (or_1_out, sSH, eSH);
  assign _8_out = eSH ? shift_register_1_q1 : 8'bz;  // Controlled_Buffer controlled_buffer_1
  // Probe on _8_out
  and and_1 (and_1_out, eSH, e16SH);
  assign _16_out = and_1_out ? {shift_register_1_q0, shift_register_1_q1} : 16'bz;  // Controlled_Buffer controlled_buffer_2
  // Probe on _16_out
endmodule

module regdec (
  input  [5:0] in_1,
  input  [1:0] EA_EB,
  input  [1:0] EA_EB_2,
  output [15:0] out_4
);

  wire [1:0] demultiplexer_1_out0, demultiplexer_1_out1, demultiplexer_1_out2, demultiplexer_1_out3,
       demultiplexer_1_out4, demultiplexer_1_out5, demultiplexer_1_out6, demultiplexer_1_out7,
       demultiplexer_2_out0, demultiplexer_2_out1, demultiplexer_2_out2, demultiplexer_2_out3,
       demultiplexer_2_out4, demultiplexer_2_out5, demultiplexer_2_out6, demultiplexer_2_out7;

  assign out_4[1:0] = demultiplexer_1_out0 | demultiplexer_2_out0;  // OR_Gate or_1, 2 bits wide
  assign out_4[3:2] = demultiplexer_1_out1 | demultiplexer_2_out1;  // OR_Gate or_2, 2 bits wide
  assign out_4[5:4] = demultiplexer_1_out2 | demultiplexer_2_out2;  // OR_Gate or_3, 2 bits wide
  assign out_4[7:6] = demultiplexer_1_out3 | demultiplexer_2_out3;  // OR_Gate or_4, 2 bits wide
  assign out_4[9:8] = demultiplexer_1_out4 | demultiplexer_2_out4;  // OR_Gate or_5, 2 bits wide
  assign out_4[11:10] = demultiplexer_1_out5 | demultiplexer_2_out5;  // OR_Gate or_6, 2 bits wide
  assign out_4[13:12] = demultiplexer_1_out6 | demultiplexer_2_out6;  // OR_Gate or_7, 2 bits wide
  assign out_4[15:14] = demultiplexer_1_out7 | demultiplexer_2_out7;  // OR_Gate or_8, 2 bits wide
  Demultiplexer #(.select(3), .width(2), .disabled(0), .enable("false")) demultiplexer_1 (
    .out0(demultiplexer_1_out0), .out1(demultiplexer_1_out1), .out2(demultiplexer_1_out2),
    .out3(demultiplexer_1_out3), .out4(demultiplexer_1_out4), .out5(demultiplexer_1_out5),
    .out6(demultiplexer_1_out6), .out7(demultiplexer_1_out7), .in({EA_EB[1], EA_EB_2[1]}), .sel(in_1[5:3]));
  // Probe on in_1[5:3]
  // Probe on in_1[2:0]
  Demultiplexer #(.select(3), .width(2), .disabled(0), .enable("false")) demultiplexer_2 (
    .out0(demultiplexer_2_out0), .out1(demultiplexer_2_out1), .out2(demultiplexer_2_out2),
    .out3(demultiplexer_2_out3), .out4(demultiplexer_2_out4), .out5(demultiplexer_2_out5),
    .out6(demultiplexer_2_out6), .out7(demultiplexer_2_out7), .in({EA_EB[0], EA_EB_2[0]}), .sel(in_1[2:0]));
endmodule

module ALU (
  input  [2:0] OP,
  input  [7:0] A_8,
  input  [15:0] A,
  input  [15:0] B,
  input  _16,
  input  Carry_in,
  output [15:0] out,
  output [3:0] C_G_E_Z
);

  wire adder_1_cout, adder_2_cout, and_2_out, and_3_out, and_4_out, not_2_out, not_3_out, not_4_out,
       not_5_out, not_6_out, not_7_out, not_8_out, subtractor_1_bout;
  wire [7:0] undriven;
  wire [15:0] adder_1_out, adder_2_out, and_1_out, multiplexer_1_out, not_1_out, or_1_out, subtractor_1_out,
       xor_1_out;

  Pull_Resistor pull_resistor_1 (.node(_16));
  Pull_Resistor pull_resistor_2 (.node(Carry_in));
  Multiplexer #(.width(16), .disabled(0), .enable("false")) multiplexer_1 (
    .in0({undriven, A_8}), .in1(A), .out(multiplexer_1_out), .sel(_16));
  Pull_Resistor pull_resistor_3 (.node(multiplexer_1_out));
  // Probe on multiplexer_1_out
  Pull_Resistor pull_resistor_4 (.node(B));
  // Probe on B
  Adder #(.width(16)) adder_1 (.a(multiplexer_1_out), .b(B), .out(adder_1_out), .cin(Carry_in), .cout(adder_1_cout));
  assign C_G_E_Z[3] = and_3_out ? adder_1_cout : 1'bz;  // Controlled_Buffer controlled_buffer_1
  Subtractor #(.width(16)) subtractor_1 (
    .a(multiplexer_1_out), .b(B), .out(subtractor_1_out), .bin(Carry_in), .bout(subtractor_1_bout));
  assign C_G_E_Z[3] = and_4_out ? subtractor_1_bout : 1'bz;  // Controlled_Buffer controlled_buffer_2
  Adder #(.width(16)) adder_2 (
    .a(16'h1), .b(multiplexer_1_out), .out(adder_2_out), .cin(Carry_in), .cout(adder_2_cout));
  assign C_G_E_Z[3] = and_2_out ? adder_2_cout : 1'bz;  // Controlled_Buffer controlled_buffer_3
  assign xor_1_out = multiplexer_1_out ^ B;  // XOR_Gate xor_1, 16 bits wide
  assign or_1_out = multiplexer_1_out | B;  // OR_Gate or_1, 16 bits wide
  assign and_1_out = multiplexer_1_out & B;  // AND_Gate and_1, 16 bits wide
  assign not_1_out = ~multiplexer_1_out;  // NOT_Gate not_1, 16 bits wide
  Comparator #(.width(16)) comparator_1 (.a(multiplexer_1_out), .b(B), .gt(C_G_E_Z[2]), .eq(C_G_E_Z[1]));  // open: lt
  Pull_Resistor pull_resistor_5 (.node(C_G_E_Z[3]));
  nor nor_1 (C_G_E_Z[0], multiplexer_1_out[0], multiplexer_1_out[1], multiplexer_1_out[2], multiplexer_1_out[3], multiplexer_1_out[4], multiplexer_1_out[5], multiplexer_1_out[6], multiplexer_1_out[7], multiplexer_1_out[8], multiplexer_1_out[9], multiplexer_1_out[10], multiplexer_1_out[11], multiplexer_1_out[12], multiplexer_1_out[13], multiplexer_1_out[14], multiplexer_1_out[15]);
  Pull_Resistor pull_resistor_6 (.node(C_G_E_Z));
  and and_2 (and_2_out, not_2_out, OP[1], not_3_out);
  and and_3 (and_3_out, not_4_out, not_5_out, not_6_out);
  and and_4 (and_4_out, OP[0], not_7_out, not_8_out);
  Pull_Resistor pull_resistor_7 (.node(OP));
  not not_2 (not_2_out, OP[0]);
  not not_3 (not_3_out, OP[2]);
  not not_4 (not_4_out, OP[0]);
  not not_5 (not_5_out, OP[1]);
  not not_6 (not_6_out, OP[2]);
  not not_7 (not_7_out, OP[1]);
  not not_8 (not_8_out, OP[2]);
  Multiplexer #(.select(3), .width(16), .disabled(0), .enable("false")) multiplexer_2 (
    .in0(adder_1_out), .in1(subtractor_1_out), .in2(adder_2_out), .in3(xor_1_out), .in4(or_1_out),
    .in5(and_1_out), .in6(not_1_out), .out(out), .sel(OP));  // open: in7
  // Probe on out
endmodule

module FLG (
  input  [3:0] in_1,
  input  [3:0] cgez,
  output t_f
);

  wire [3:0] and_1_out;

  // Probe on and_1_out
  assign and_1_out = in_1 & cgez;  // AND_Gate and_1, 4 bits wide
  or or_1 (t_f, and_1_out[0], and_1_out[1], and_1_out[2], and_1_out[3]);
endmodule

module _16_1_reg (
  input  [15:0] _16_in,
  input  [7:0] _8_in,
  input  [2:0] _16_S_E,
  output [15:0] _16_out,
  output [7:0] _8_out
);

  wire [15:0] multiplexer_1_out, register_1_q;
  wire [15:8] demultiplexer_1_out0;

  Multiplexer #(.width(16), .disabled(0), .enable("false")) multiplexer_1 (
    .in0({{8{1'b0}}, _8_in}), .in1(_16_in), .out(multiplexer_1_out), .sel(_16_S_E[2]));
  Register #(.width(16)) register_1 (.D(multiplexer_1_out), .Q(register_1_q), .clk(_16_S_E[1]));  // open: en, clr
  Demultiplexer #(.width(16), .tristate("true")) demultiplexer_1 (
    .out0({demultiplexer_1_out0, _8_out}), .out1(_16_out), .in(register_1_q), .sel(_16_S_E[2]),
    .en(_16_S_E[0]));
endmodule
